# Fritzing sketch ReactionDiagram01 (saved by Fritzing 0.9.3b)
breadboards: 1

parts:
  Raspberry_Pi_1 = Raspberry Pi 3 [part_number=RPI-3-V1.2]
  S1 = Momentary Switch [package=ksa_sealed_tac_switch]
  S2 = Momentary Switch [package=ksa_sealed_tac_switch]
  LED2 = LED - 3mm [color="Red (633nm)" package="3 mm [THT]"]
  R1 = Resistor [tolerance=±5% resistance=220 package="0603 [SMD]"]

nets:
  N1: Raspberry_Pi_1.GIPO25, S2.3
  N2: Raspberry_Pi_1.GND, S1.1, S2.1, LED2.cathode, R1.Pin_0, R1.Pin_1
  N3: Raspberry_Pi_1.GIPO18, LED2.anode
  N4: Raspberry_Pi_1.GIPO14, S1.3
